// Logisim project s-mips.circ as structural Verilog
module S_MIPS_Board (
  input  DESHABILITAR_DISPATCHER,
  output halt
);

  wire button_1_out, CLK, CS, d_ff_1_q, LCLR, LoadRAM, LoadRAMOn, LW, R_R_W, R_W, ram_dispatcher_1_finished,
       RCS, Reset_out, RST, TTY_EN;
  wire [2:0] KDB;
  wire [3:0] LMask, Mask, ram_1_read_time, ram_1_write_time, RMask;
  wire [6:0] KDB_DATA, TTY_DATA;
  wire [15:0] Addr, LAddr, RAddr;
  wire [31:0] I0, I1, I2, I3, LData, ram_1_data_out_0, ram_1_data_out_1, ram_1_data_out_2, ram_1_data_out_3,
       RI0, RI1, RI2, RI3;

  TTY #(.rows(25), .cols(80)) tty_1 (.data(TTY_DATA), .clk(CLK), .we(TTY_EN), .clr(RST));
  not not_1 (LoadRAMOn, ram_dispatcher_1_finished);
  RAM_Dispatcher ram_dispatcher_1 (
    .WriteTime(ram_1_write_time), .Clock(CLK), .Data(LData), .Address(LAddr), .Mask(LMask),
    .Finished(ram_dispatcher_1_finished), .Write(LW), .CLR(LCLR));
  Keyboard #(.buflen(64)) keyboard_1 (.clk(CLK), .re(KDB[0]), .avail(KDB[2]), .data(KDB_DATA));  // open: clr
  RAM ram_1 (
    .Address(RAddr), .Data_Out_0(ram_1_data_out_0), .Data_Out_1(ram_1_data_out_1),
    .Data_Out_2(ram_1_data_out_2), .Data_Out_3(ram_1_data_out_3), .Data_In_0(RI0), .Data_In_1(RI1),
    .Data_In_2(RI2), .Data_In_3(RI3), .Mask(RMask), .nRead_Write(R_R_W), .Chip_Select(RCS),
    .Read_Time(ram_1_read_time), .Reset(button_1_out), .Write_Time(ram_1_write_time));
  Button button_1 (.out(button_1_out));
  D_Flip_Flop d_ff_1 (.clk(CLK), .D(1'b1), .Q(d_ff_1_q), .reset(Reset_out));  // open: Qn, preset, en
  Button Reset (.out(Reset_out));
  S_MIPS s_mips_1 (
    .Kbd_Enable(KDB[0]), .Address(Addr), .Kbd_Clear(KDB[1]), .Kbd_Available(KDB[2]), .RAM_In_0(I0),
    .Kbd_ASCII_Data(KDB_DATA), .RAM_In_1(I1), .TTY_Enable(TTY_EN), .RAM_In_2(I2), .RAM_In_3(I3),
    .TTY_ASCII_Data(TTY_DATA), .Reset(RST), .RAM_Out_0(ram_1_data_out_0), .Clock(CLK),
    .RAM_Out_1(ram_1_data_out_1), .Stop(halt), .RAM_Out_2(ram_1_data_out_2), .RAM_Out_3(ram_1_data_out_3),
    .Mask(Mask), .Read_Time(ram_1_read_time), .Write_Time(ram_1_write_time), .nRead_Write(R_W),
    .Chip_Select(CS));
  D_Flip_Flop d_ff_2 (.clk(CLK), .D(d_ff_1_q), .Qn(LCLR), .reset(Reset_out));  // open: Q, preset, en
  or or_1 (RST, LCLR, LoadRAM);
  Clock clock_1 (.out(CLK));
  Multiplexer #(.width(32), .enable("false")) multiplexer_1 (.in0(I0), .in1(LData), .out(RI0), .sel(LoadRAM));
  Multiplexer #(.width(32), .enable("false")) multiplexer_2 (.in0(I1), .in1(LData), .out(RI1), .sel(LoadRAM));
  Multiplexer #(.width(32), .enable("false")) multiplexer_3 (.in0(I2), .in1(LData), .out(RI2), .sel(LoadRAM));
  Multiplexer #(.width(32), .enable("false")) multiplexer_4 (.in0(I3), .in1(LData), .out(RI3), .sel(LoadRAM));
  and and_1 (LoadRAM, ~1'b1, LoadRAMOn);  // AND_Gate
  Multiplexer #(.width(16), .enable("false")) multiplexer_5 (.in0(Addr), .in1(LAddr), .out(RAddr), .sel(LoadRAM));
  Multiplexer #(.width(4), .enable("false")) multiplexer_6 (.in0(Mask), .in1(LMask), .out(RMask), .sel(LoadRAM));
  Multiplexer #(.enable("false")) multiplexer_7 (.in0(CS), .in1(LW), .out(RCS), .sel(LoadRAM));
  Multiplexer #(.enable("false")) multiplexer_8 (.in0(R_W), .in1(LW), .out(R_R_W), .sel(LoadRAM));

  // Notes on the sheet:
  //   NO MODIFICAR
  //   Keyboard
endmodule

module S_MIPS (
  input  Kbd_Available,
  input  [6:0] Kbd_ASCII_Data,
  input  [31:0] RAM_Out_0,
  input  [31:0] RAM_Out_1,
  input  Reset,
  input  [31:0] RAM_Out_2,
  input  Clock,
  input  [31:0] RAM_Out_3,
  input  [3:0] Read_Time,
  input  [3:0] Write_Time,
  output Kbd_Enable,
  output [15:0] Address,
  output Kbd_Clear,
  output TTY_Enable,
  output [6:0] TTY_ASCII_Data,
  output Stop,
  output [31:0] RAM_In_0,
  output [31:0] RAM_In_1,
  output [31:0] RAM_In_2,
  output [31:0] RAM_In_3,
  output [3:0] Mask,
  output nRead_Write,
  output Chip_Select
);

  wire not_1_out;

  not not_1 (not_1_out, Reset);
  CPU___Final cpu_final_1 (
    .WT(Write_Time), .RT(Read_Time), .clk(Clock), .start(not_1_out), .rst(Reset), .D1(RAM_Out_0),
    .D2(RAM_Out_1), .D3(RAM_Out_2), .D4(RAM_Out_3), .TTY_ENABLE(TTY_Enable), .D_Out(RAM_In_0),
    .TTY_DATA(TTY_ASCII_Data), .END(Stop), .RAM_Adress(Address), .CS(Chip_Select), .RAM_R_W(nRead_Write),
    .MASK(Mask), .in_10(Kbd_Available), .in_11(Kbd_ASCII_Data), .kbd_En(Kbd_Enable));

  assign RAM_In_1 = RAM_In_0;
  assign RAM_In_2 = RAM_In_0;
  assign RAM_In_3 = RAM_In_0;

  // Other names for the same wires on the sheet: CLK = Clock; CLR = Reset; CS = Chip_Select;
  //   KBD_AVAIL = Kbd_Available; KBD_CLR = Kbd_Clear; KBD_DATA[6:0] = Kbd_ASCII_Data; RAM_A[15:0] = Address;
  //   RAM_INPUT_0[31:0] = RAM_In_0; RAM_INPUT_1[31:0] = RAM_In_0; RAM_INPUT_2[31:0] = RAM_In_0;
  //   RAM_INPUT_3[31:0] = RAM_In_0; RAM_MASK[3:0] = Mask; RAM_OUTPUT_0[31:0] = RAM_Out_0;
  //   RAM_OUTPUT_1[31:0] = RAM_Out_1; RAM_OUTPUT_2[31:0] = RAM_Out_2; RAM_OUTPUT_3[31:0] = RAM_Out_3;
  //   RW = nRead_Write; TTY_DATA[6:0] = TTY_ASCII_Data

  // Notes on the sheet:
  //   RAM ADDRESS
  //   DATA FROM RAM
  //   DATA TO RAM
  //   DATA WRITE MASK
  //   RAM TIMING
  //   RAM CONTROL
  //   KEYBOARD
  //   TTY
  //   SEQUENCING
endmodule

module RAM (
  input  [15:0] Address,
  input  [31:0] Data_In_0,
  input  [31:0] Data_In_1,
  input  [31:0] Data_In_2,
  input  [31:0] Data_In_3,
  input  [3:0] Mask,
  input  nRead_Write,
  input  Chip_Select,
  input  Reset,
  output [31:0] Data_Out_0,
  output [31:0] Data_Out_1,
  output [31:0] Data_Out_2,
  output [31:0] Data_Out_3,
  output [3:0] Read_Time,
  output [3:0] Write_Time
);

  wire and_2_out, and_3_out, and_4_out, and_5_out, and_6_out, and_7_out, and_8_out, and_9_out, Changed, CLK,
       comparator_2_eq, comparator_3_eq, comparator_4_eq, comparator_5_eq, comparator_6_eq, Count,
       demultiplexer_3_out0, Idle, Idle_q, Load, Load0, Load1, nand_1_out, or_1_out, or_2_out, or_3_out,
       or_4_out, or_5_out, or_6_out, or_7_out, or_8_out, or_9_out, or_10_out, Proc_q, Update_Mem, Zero_Time;
  wire [3:0] counter_1_q, multiplexer_1_out, subtractor_1_out;
  wire [31:0] register_1_q, register_2_q, register_3_q, register_4_q, register_5_q;

  // Probe on 4'b0011
  // Probe on 4'b0010
  Multiplexer #(.width(4), .enable("false")) multiplexer_1 (
    .in0(4'b0011), .in1(4'b0010), .out(multiplexer_1_out), .sel(nRead_Write));
  or or_1 (or_1_out, Idle, Update_Mem);
  or or_2 (or_2_out, ~Chip_Select, Reset);  // OR_Gate
  Subtractor #(.width(4)) subtractor_1 (.a(multiplexer_1_out), .b(4'b0010), .out(subtractor_1_out));  // open: bin, bout
  D_Flip_Flop u_Idle (.clk(CLK), .D(or_1_out), .Q(Idle_q), .preset(or_2_out));  // open: Qn, en, reset
  Demultiplexer #(.enable("false")) demultiplexer_1 (.out0(Idle), .out1(Load0), .in(Idle_q), .sel(Changed));
  // Probe on counter_1_q
  Counter #(.width(4), .max('hf)) counter_1 (
    .load(Load), .D(subtractor_1_out), .count(Count), .Q(counter_1_q), .clk(CLK), .clr(or_3_out));  // open: carry
  or or_3 (or_3_out, ~Chip_Select, Reset);  // OR_Gate
  Comparator #(.width(4), .mode("unsigned")) comparator_1 (
    .a(4'b0000), .b(counter_1_q), .eq(Zero_Time));  // open: gt, lt
  or or_4 (or_4_out, Count, Load0, Load1);
  Register #(.width(32)) register_1 (.D(Data_In_0), .en(Chip_Select), .Q(register_1_q), .clk(CLK), .clr(or_5_out));
  or or_5 (or_5_out, ~Chip_Select, Reset);  // OR_Gate
  Register #(.width(32)) register_2 (.D(Data_In_1), .en(Chip_Select), .Q(register_2_q), .clk(CLK), .clr(or_6_out));
  or or_6 (or_6_out, ~Chip_Select, Reset);  // OR_Gate
  Register #(.width(32)) register_3 (.D(Data_In_2), .en(Chip_Select), .Q(register_3_q), .clk(CLK), .clr(or_7_out));
  or or_7 (or_7_out, ~Chip_Select, Reset);  // OR_Gate
  Register #(.width(32)) register_4 (.D(Data_In_3), .en(Chip_Select), .Q(register_4_q), .clk(CLK), .clr(or_8_out));
  or or_8 (or_8_out, ~Chip_Select, Reset);  // OR_Gate
  Register #(.width(32)) register_5 (
    .D({{11{1'b1}}, nRead_Write, Mask, Address}), .en(Chip_Select), .Q(register_5_q), .clk(CLK),
    .clr(or_9_out));
  or or_9 (or_9_out, ~Chip_Select, Reset);  // OR_Gate
  D_Flip_Flop Proc (.clk(CLK), .D(or_4_out), .Q(Proc_q), .reset(or_10_out));  // open: Qn, preset, en
  or or_10 (or_10_out, ~Chip_Select, Reset);  // OR_Gate
  Demultiplexer #(.enable("false")) demultiplexer_2 (
    .out0(Count), .out1(Update_Mem), .in(demultiplexer_3_out0), .sel(Zero_Time));
  Demultiplexer #(.enable("false")) demultiplexer_3 (
    .out0(demultiplexer_3_out0), .out1(Load1), .in(Proc_q), .sel(Changed));
  Clock clock_1 (.out(CLK));
  Comparator #(.width(32)) comparator_2 (.a(register_1_q), .b(Data_In_0), .eq(comparator_2_eq));  // open: gt, lt
  Comparator #(.width(32)) comparator_3 (.a(register_2_q), .b(Data_In_1), .eq(comparator_3_eq));  // open: gt, lt
  Comparator #(.width(32)) comparator_4 (.a(register_3_q), .b(Data_In_2), .eq(comparator_4_eq));  // open: gt, lt
  Comparator #(.width(32)) comparator_5 (.a(register_4_q), .b(Data_In_3), .eq(comparator_5_eq));  // open: gt, lt
  Comparator #(.width(32)) comparator_6 (
    .a(register_5_q), .b({{11{1'b1}}, nRead_Write, Mask, Address}), .eq(comparator_6_eq));  // open: gt, lt
  nand nand_1 (nand_1_out, comparator_6_eq, comparator_2_eq, comparator_3_eq, comparator_4_eq, comparator_5_eq);
  and and_1 (Changed, nand_1_out, Chip_Select);
  or or_11 (Load, Count, Load1, Load0);
  and and_2 (and_2_out, Mask[0], Update_Mem, nRead_Write);
  and and_3 (and_3_out, Mask[1], Update_Mem, nRead_Write);
  and and_4 (and_4_out, Mask[2], Update_Mem, nRead_Write);
  and and_5 (and_5_out, Mask[3], Update_Mem, nRead_Write);
  RAM_part #(.addrWidth(16), .dataWidth(32), .bus("separate")) ram_1 (
    .addr(Address), .din(Data_In_0), .data(Data_Out_0), .str(and_2_out), .sel(Chip_Select), .clk(CLK),
    .ld(and_6_out), .clr(Reset));
  and and_6 (and_6_out, ~nRead_Write, Idle);  // AND_Gate
  RAM_part #(.addrWidth(16), .dataWidth(32), .bus("separate")) ram_2 (
    .addr(Address), .din(Data_In_1), .data(Data_Out_1), .str(and_3_out), .sel(Chip_Select), .clk(CLK),
    .ld(and_7_out), .clr(Reset));
  and and_7 (and_7_out, ~nRead_Write, Idle);  // AND_Gate
  RAM_part #(.addrWidth(16), .dataWidth(32), .bus("separate")) ram_3 (
    .addr(Address), .din(Data_In_2), .data(Data_Out_2), .str(and_4_out), .sel(Chip_Select), .clk(CLK),
    .ld(and_8_out), .clr(Reset));
  and and_8 (and_8_out, ~nRead_Write, Idle);  // AND_Gate
  RAM_part #(.addrWidth(16), .dataWidth(32), .bus("separate")) ram_4 (
    .addr(Address), .din(Data_In_3), .data(Data_Out_3), .str(and_5_out), .sel(Chip_Select), .clk(CLK),
    .ld(and_9_out), .clr(Reset));
  and and_9 (and_9_out, ~nRead_Write, Idle);  // AND_Gate

  assign Read_Time = 4'b0011;
  assign Write_Time = 4'b0010;

  // Other names for the same wires on the sheet: M0 = Mask[0]; M1 = Mask[1]; M2 = Mask[2]; M3 = Mask[3];
  //   RW = nRead_Write; CLR = Reset; CS = Chip_Select; Load2 = Count

  // Notes on the sheet:
  //   NO MODIFICAR
  //   excepto quizás los valores RT y WT
  //   BANK0
  //   BANK1
  //   BANK2
  //   BANK3
endmodule

module RAM_Dispatcher (
  input  [3:0] WriteTime,
  input  Clock,
  input  CLR,
  output [31:0] Data,
  output [15:0] Address,
  output [3:0] Mask,
  output Finished,
  output Write
);

  wire demultiplexer_2_out1, demultiplexer_3_out1, End, IDLE_q, IncAddr, Load, or_1_out, or_2_out, While_q,
       WriteEnd;
  wire [3:0] counter_1_q;
  wire [31:0] CurrentAddress_q;

  Counter #(.width(32), .max('hffffffff)) CurrentAddress (
    .count(IncAddr), .Q({CurrentAddress_q[31:18], Address, CurrentAddress_q[1:0]}), .clk(Clock), .clr(CLR));  // open: load, D, carry
  or or_1 (or_1_out, IncAddr, demultiplexer_3_out1, Finished);
  D_Flip_Flop IDLE (.clk(Clock), .D(or_1_out), .Q(IDLE_q), .preset(CLR));  // open: Qn, en, reset
  Demultiplexer #(.enable("false")) demultiplexer_1 (.out0(Load), .out1(Finished), .in(IDLE_q), .sel(End));
  D_Flip_Flop While (.clk(Clock), .D(or_2_out), .Q(While_q), .reset(CLR));  // open: Qn, preset, en
  or or_2 (or_2_out, Write, Load);
  RAM_part #(.addrWidth(18), .dataWidth(32)) ram_1 (
    .addr({Address, CurrentAddress_q[1:0]}), .data(Data), .clk(Clock));  // open: sel, ld, clr
  Demultiplexer #(.enable("false")) demultiplexer_2 (
    .out0(Write), .out1(demultiplexer_2_out1), .in(While_q), .sel(WriteEnd));
  Decoder #(.select(2)) decoder_1 (
    .out0(Mask[0]), .out1(Mask[1]), .out2(Mask[2]), .out3(Mask[3]), .sel(CurrentAddress_q[1:0]));  // open: en
  Demultiplexer #(.enable("false")) demultiplexer_3 (
    .out0(IncAddr), .out1(demultiplexer_3_out1), .in(demultiplexer_2_out1), .sel(End));
  Counter #(.width(4), .max('hf)) counter_1 (
    .load(Load), .D(WriteTime), .count(Write), .Q(counter_1_q), .clk(Clock));  // open: carry, clr
  Comparator #(.width(32)) comparator_1 (.a(Data), .b({32{1'b1}}), .eq(End));  // open: gt, lt
  Comparator #(.width(4)) comparator_2 (.a(4'b0000), .b(counter_1_q), .eq(WriteEnd));  // open: gt, lt

  // Other names for the same wires on the sheet: CLK = Clock; Count = Write; WT[3:0] = WriteTime
endmodule

module CPU___Final (
  input  [3:0] WT,
  input  [3:0] RT,
  input  clk,
  input  start,
  input  rst,
  input  [31:0] D1,
  input  [31:0] D2,
  input  [31:0] D3,
  input  [31:0] D4,
  input  in_10,
  input  [6:0] in_11,
  output kbd_En,
  output TTY_ENABLE,
  output [31:0] D_Out,
  output [6:0] TTY_DATA,
  output END,
  output [15:0] RAM_Adress,
  output CS,
  output RAM_R_W,
  output [3:0] MASK
);

  wire D_Load, Hi_Lo_Sel, HiLo_Load, I, IR_Load, J, jr, L_En, PC_En, pop_2, push, R, RF_R_W;
  wire [1:0] ALU_A, ALU_B, RF_D_SEL;
  wire [3:0] ALU_Op;
  wire [5:0] func_code, op_code;

  Control_Unit control_unit_1 (
    .DATA_Load(D_Load), .in_1(clk), .in_2(RT), .in_3(WT), .in_4(rst), .in_5(start), .in_6(R), .in_7(op_code),
    .in_8(I), .in_9(func_code), .in_10(J), .END(END), .PC_Load(PC_En), .Sel_A(ALU_A), .Loads_Enable(L_En),
    .Sel_B(ALU_B), .ALU_OP(ALU_Op), .CS(CS), .out_22(Hi_Lo_Sel), .out_23(HiLo_Load), .out_24(jr),
    .out_27(push), .tty(TTY_ENABLE), .IR_Load(IR_Load), .out_25(RF_D_SEL), .out_26(RF_R_W), .pop2(pop_2),
    .RAM_R_W(RAM_R_W), .kbd_En(kbd_En));
  DataPath___main datapath_main_1 (
    .in_1(push), .in_2(ALU_Op), .in_3(D1), .in_4(pop_2), .in_5(ALU_A), .in_6(jr), .in_7(ALU_B), .in_8(D2),
    .in_9(RF_R_W), .in_10(HiLo_Load), .in_11(RF_D_SEL), .in_12(Hi_Lo_Sel), .in_15(D_Load), .in_13(D3),
    .in_16(L_En), .in_17(IR_Load), .in_18(clk), .in_19(D_Load), .in_21(rst), .in_22(PC_En), .in_20(D4),
    .out_25(func_code), .out_26(op_code), .TTY_DATA(TTY_DATA), .out_29(I), .out_30(J), .out_31(R),
    .D_RAM_OUT(D_Out), .in_14(RAM_R_W), .RAM_DIR(RAM_Adress), .MASK(MASK), .in_23(in_11), .in_24(in_10));

  // Other names for the same wires on the sheet: D_To_RAM[31:0] = D_Out; KBD_AV = in_10; KBD_DATA[6:0] = in_11;
  //   RAM_Adr[15:0] = RAM_Adress; TTY_En = TTY_ENABLE

  // Notes on the sheet:
  //   RAM TIME
  //   CPU - ASM
  //   RAM DATA IN
  //   KEYBOARD IN
  //   RAM OUT
  //   SCREEN
endmodule

module Control_Unit (
  input  in_1,
  input  [3:0] in_2,
  input  [3:0] in_3,
  input  in_4,
  input  in_5,
  input  in_6,
  input  [5:0] in_7,
  input  in_8,
  input  [5:0] in_9,
  input  in_10,
  output END,
  output PC_Load,
  output IR_Load,
  output pop2,
  output DATA_Load,
  output [1:0] Sel_A,
  output Loads_Enable,
  output [1:0] Sel_B,
  output [3:0] ALU_OP,
  output tty,
  output CS,
  output out_22,
  output out_23,
  output out_24,
  output [1:0] out_25,
  output out_26,
  output out_27,
  output RAM_R_W,
  output kbd_En
);

  wire d_ff_1_q, demultiplexer_1_out0, demultiplexer_1_out1, demultiplexer_2_out0, demultiplexer_3_out0,
       demultiplexer_3_out1, demultiplexer_4_out0, demultiplexer_4_out1, demultiplexer_6_out0,
       demultiplexer_6_out1, demultiplexer_7_out1, end_R0, end_R1, end_W, EXECUTE_q, FETCH_q, is_halt,
       Loads_En0, Loads_En1, Loads_En3, lw, or_1_out, or_2_out, or_3_out, or_7_out, or_8_out, or_9_out, pop,
       R_RAM, sw, USE_RAM_0, USE_RAM_1, USE_RAM_2, WAIT_2_q, WAIT_4_q;
  wire [3:0] ALU_SEL;

  D_Flip_Flop d_ff_1 (.clk(in_1), .D(demultiplexer_1_out0), .Q(d_ff_1_q), .preset(in_4));  // open: Qn, en, reset
  Demultiplexer #(.disabled(0), .enable("false")) demultiplexer_1 (
    .out0(demultiplexer_1_out0), .out1(demultiplexer_1_out1), .in(d_ff_1_q), .sel(in_5));
  or or_1 (or_1_out, PC_Load, demultiplexer_1_out1);
  D_Flip_Flop FETCH (.clk(in_1), .D(or_1_out), .Q(FETCH_q), .reset(in_4));  // open: Qn, preset, en
  or or_2 (or_2_out, demultiplexer_2_out0, FETCH_q);
  Get_Signals get_signals_1 (
    .R(in_6), .I(in_8), .J(in_10), .Op_Code(in_7), .Func_Code(in_9), .Push(out_27), .HiLo_Sel(out_22),
    .RF_Sel(out_25), .Load_HiLo(out_23), .RF_R_W(out_26), .Halt(is_halt), .tty(tty), .Pop(pop), .Jr(out_24),
    .R_Ram(R_RAM), .W_Ram(RAM_R_W), .lw(lw), .sw(sw), .KBD_En(kbd_En));
  Demultiplexer #(.disabled(0), .enable("false")) demultiplexer_2 (
    .out0(demultiplexer_2_out0), .out1(IR_Load), .in(USE_RAM_0), .sel(end_R0));
  D_Flip_Flop \wait  (.clk(in_1), .D(or_2_out), .Q(USE_RAM_0), .reset(in_4));  // open: Qn, preset, en
  Waiter waiter_1 (.in_1(in_2), .\end (end_R0), .in_2(in_1), .in_3(PC_Load), .in_4(FETCH_q));
  Demultiplexer #(.disabled(0), .enable("false")) demultiplexer_3 (
    .out0(demultiplexer_3_out0), .out1(demultiplexer_3_out1), .in(EXECUTE_q), .sel(is_halt));
  D_Flip_Flop EXECUTE (.clk(in_1), .D(IR_Load), .Q(EXECUTE_q), .reset(in_4));  // open: Qn, preset, en
  or or_3 (or_3_out, END, demultiplexer_3_out1);
  Demultiplexer #(.disabled(0), .enable("false")) demultiplexer_4 (
    .out0(demultiplexer_4_out0), .out1(demultiplexer_4_out1), .in(demultiplexer_3_out0), .sel(R_RAM));
  ALU_Decoder alu_decoder_1 (
    .in_1(in_7), .in_2(in_9), .in_3(in_6), .in_4(in_8), .in_5(in_10), .ALU_SEL(ALU_SEL), .Sel_A(Sel_A),
    .Sel_B(Sel_B), .Pop(pop), .Push(out_27), .lw(lw), .sw(sw));
  D_Flip_Flop u_END (.clk(in_1), .D(or_3_out), .Q(END), .reset(in_4));  // open: Qn, preset, en
  or or_4 (DATA_Load, USE_RAM_1, demultiplexer_4_out1);
  Waiter waiter_2 (.in_1(in_2), .\end (end_R1), .in_2(in_1), .in_3(PC_Load), .in_4(demultiplexer_4_out1));
  D_Flip_Flop WAIT_2 (.clk(in_1), .D(DATA_Load), .Q(WAIT_2_q), .reset(in_4));  // open: Qn, preset, en
  Demultiplexer #(.disabled(0), .enable("false")) demultiplexer_5 (
    .out0(USE_RAM_1), .out1(Loads_En1), .in(WAIT_2_q), .sel(end_R1));
  Demultiplexer #(.disabled(0), .enable("false")) demultiplexer_6 (
    .out0(demultiplexer_6_out0), .out1(demultiplexer_6_out1), .in(Loads_En1), .sel(pop));
  or or_5 (Loads_Enable, Loads_En0, Loads_En1, pop2, Loads_En3);
  or or_6 (CS, USE_RAM_0, USE_RAM_1, USE_RAM_2);
  D_Flip_Flop WAIT_3 (.clk(in_1), .D(demultiplexer_6_out1), .Q(pop2), .reset(in_4));  // open: Qn, preset, en
  Multiplexer #(.width(4), .disabled(0), .enable("false")) multiplexer_1 (
    .in0(ALU_SEL), .in1(4'b0000), .out(ALU_OP), .sel(pop2));
  Demultiplexer #(.disabled(0), .enable("false")) demultiplexer_7 (
    .out0(Loads_En0), .out1(demultiplexer_7_out1), .in(or_7_out), .sel(RAM_R_W));
  or or_7 (or_7_out, demultiplexer_4_out0, demultiplexer_6_out0, pop2);
  or or_8 (or_8_out, USE_RAM_2, demultiplexer_7_out1);
  D_Flip_Flop WAIT_4 (.clk(in_1), .D(or_8_out), .Q(WAIT_4_q), .reset(in_4));  // open: Qn, preset, en
  Waiter waiter_3 (.in_1(in_3), .\end (end_W), .in_2(in_1), .in_3(PC_Load), .in_4(demultiplexer_7_out1));
  Demultiplexer #(.disabled(0), .enable("false")) demultiplexer_8 (
    .out0(USE_RAM_2), .out1(Loads_En3), .in(WAIT_4_q), .sel(end_W));
  or or_9 (or_9_out, Loads_En0, Loads_En3);
  D_Flip_Flop NEXT (.clk(in_1), .D(or_9_out), .Q(PC_Load), .reset(in_4));  // open: Qn, preset, en

  // Other names for the same wires on the sheet: clk = in_1; func_code[5:0] = in_9; I = in_8; J = in_10; jr = out_24;
  //   op_code[5:0] = in_7; push = out_27; R = in_6; rst = in_4; rst_w = PC_Load; RT[3:0] = in_2; Loads_En2 = pop2;
  //   SP___4 = pop2; start = in_5; W_RAM = RAM_R_W; WT[3:0] = in_3
endmodule

module Waiter (
  input  [3:0] in_1,
  input  in_2,
  input  in_3,
  input  in_4,
  output \end 
);

  wire comparator_1_lt, count, s;
  wire [3:0] i, t___1;

  D_Flip_Flop d_ff_1 (.clk(in_2), .Q(s), .preset(in_4), .reset(in_3));  // open: D, Qn, en
  Counter #(.width(4), .max('hf), .ongoal("stay")) counter (
    .count(count), .Q(i), .clk(in_2), .clr(in_3));  // open: load, D, carry
  and and_1 (count, s, ~\end );  // AND_Gate
  Adder #(.width(4)) adder_1 (.a(in_1), .b(4'b0001), .out(t___1));  // open: cin, cout
  Comparator #(.width(4), .mode("unsigned")) comparator_1 (.a(i), .b(t___1), .lt(comparator_1_lt));  // open: gt, eq
  not not_1 (\end , comparator_1_lt);

  // Other names for the same wires on the sheet: clk = in_2; rst = in_3; start = in_4; t[3:0] = in_1

  // Notes on the sheet:
  //   WAITER
endmodule

module ALU_Decoder (
  input  [5:0] in_1,
  input  [5:0] in_2,
  input  in_3,
  input  in_4,
  input  in_5,
  input  Pop,
  input  Push,
  input  lw,
  input  sw,
  output [3:0] ALU_SEL,
  output [1:0] Sel_A,
  output [1:0] Sel_B
);

  wire addi, and_2_out, and_3_out, and_4_out, andi, B___00, B___10, beq, bge, bgtz, bltz, bne,
       comparator_7_eq, decoder_1_out11, do_A, mfhi, mflo, Op_00, or_1_out, or_2_out, or_3_out, or_7_out,
       or_8_out, or_9_out, or_10_out, ori, slt, slti, sltiu, sltu, \xor , xorii;
  wire [3:0] ALU_SEL_I, ALU_SEL_R, multiplexer_1_out, multiplexer_2_out, multiplexer_4_out, multiplexer_5_out;

  Decoder #(.select(4), .enable("false")) decoder_1 (
    .out1(bltz), .out4(beq), .out5(bne), .out6(bge), .out7(bgtz), .out8(addi), .out10(slti),
    .out11(decoder_1_out11), .out12(andi), .out13(ori), .out14(xorii), .sel(in_1[3:0]));  // open: out0, out2, out3, out9, out15
  and and_1 (sltiu, decoder_1_out11, Op_00);
  // Probe on 6'b101000
  // Probe on 6'b101010
  // Probe on 6'b101011
  // Probe on 6'b010000
  // Probe on 6'b010010
  or or_1 (or_1_out, beq, bne);
  or or_2 (or_2_out, bge, bltz, bgtz);
  Comparator #(.width(6), .mode("unsigned")) comparator_1 (.a(in_2), .b(6'b101000), .eq(\xor ));  // open: gt, lt
  Comparator #(.width(6), .mode("unsigned")) comparator_2 (.a(in_2), .b(6'b101010), .eq(slt));  // open: gt, lt
  Comparator #(.width(6), .mode("unsigned")) comparator_3 (.a(in_2), .b(6'b101011), .eq(sltu));  // open: gt, lt
  Comparator #(.width(6), .mode("unsigned")) comparator_4 (.a(in_2), .b(6'b010000), .eq(mfhi));  // open: gt, lt
  Comparator #(.width(6), .mode("unsigned")) comparator_5 (.a(in_2), .b(6'b010010), .eq(mflo));  // open: gt, lt
  or or_3 (or_3_out, addi, lw, sw);
  // Probe on 4'b0110
  Priority_Encoder #(.select(4), .disabled(0)) priority_encoder_1 (
    .in0(or_3_out), .in2(or_1_out), .in4(andi), .in5(ori), .in6(xorii), .in12(slti), .in13(sltiu),
    .in15(or_2_out), .out(ALU_SEL_I));  // open: in1, in3, in7, in8, in9, in10, in11, in14, gs, en_out, en_in
  Multiplexer #(.width(4), .disabled(0), .enable("false")) multiplexer_1 (
    .in0(in_2[3:0]), .in1(4'b0110), .out(multiplexer_1_out), .sel(\xor ));
  Multiplexer #(.width(4), .disabled(0), .enable("false")) multiplexer_2 (
    .in0(multiplexer_1_out), .in1(4'b1100), .out(multiplexer_2_out), .sel(slt));
  or or_4 (do_A, mfhi, mflo, Pop);
  Multiplexer #(.width(4), .disabled(0), .enable("false")) multiplexer_3 (
    .in0(ALU_SEL_R), .in1(ALU_SEL_I), .out(ALU_SEL), .sel(in_4));
  Multiplexer #(.width(4), .disabled(0), .enable("false")) multiplexer_4 (
    .in0(multiplexer_2_out), .in1(4'b1101), .out(multiplexer_4_out), .sel(sltu));
  Comparator #(.width(2), .mode("unsigned")) comparator_6 (.a(in_1[5:4]), .b(2'b00), .eq(Op_00));  // open: gt, lt
  Comparator #(.width(2), .mode("unsigned")) comparator_7 (
    .a(in_2[5:4]), .b(2'b01), .eq(comparator_7_eq));  // open: gt, lt
  or or_5 (B___00, beq, bne);
  Multiplexer #(.width(4), .disabled(0), .enable("false")) multiplexer_5 (
    .in0(multiplexer_4_out), .in1(4'b1111), .out(multiplexer_5_out), .sel(do_A));
  and and_2 (and_2_out, Op_00, in_3);
  and and_3 (and_3_out, comparator_7_eq, in_3, Op_00);
  or or_6 (B___10, addi, andi, ori, xorii, slti);
  Multiplexer #(.width(4), .disabled(0), .enable("false")) multiplexer_6 (
    .in0(multiplexer_5_out), .in1(4'b0010), .out(ALU_SEL_R), .sel(Push));
  or or_7 (or_7_out, in_4, and_2_out);
  and and_4 (and_4_out, Op_00, in_3);
  or or_8 (or_8_out, B___10, and_3_out);
  Priority_Encoder #(.select(2), .disabled(0)) priority_encoder_2 (
    .in0(or_7_out), .in2(and_3_out), .out(Sel_A));  // open: in1, in3, gs, en_out, en_in
  or or_9 (or_9_out, and_4_out, B___00);
  Priority_Encoder #(.select(2), .disabled(0)) priority_encoder_3 (
    .in0(or_9_out), .in2(or_8_out), .in3(or_10_out), .out(Sel_B));  // open: in1, gs, en_out, en_in
  or or_10 (or_10_out, bge, bgtz, bltz);

  // Other names for the same wires on the sheet: Four[3:0] = in_2[3:0]; func_code[5:0] = in_2; Two[1:0] = in_2[5:4];
  //   I = in_4; J = in_5; op_code[5:0] = in_1; OP_Four[3:0] = in_1[3:0]; OP_Two[1:0] = in_1[5:4]; R = in_3

  // Notes on the sheet:
  //   ALU SEL
endmodule

module Get_Signals (
  input  R,
  input  I,
  input  J,
  input  [5:0] Op_Code,
  input  [5:0] Func_Code,
  output Push,
  output Halt,
  output tty,
  output Pop,
  output Jr,
  output R_Ram,
  output W_Ram,
  output HiLo_Sel,
  output [1:0] RF_Sel,
  output Load_HiLo,
  output lw,
  output RF_R_W,
  output sw,
  output KBD_En
);

  wire and_6_out, and_11_out, comparator_3_eq, comparator_4_eq, comparator_5_eq, comparator_6_eq,
       comparator_7_lt, comparator_8_gt, comparator_9_lt, comparator_10_eq, comparator_11_eq,
       comparator_12_gt, comparator_13_lt, comparator_16_eq, comparator_17_eq, FC___1, mfhi, nor_1_out,
       not_1_out, OP___0, OP___0_t, OP___63, or_4_out, rnd, Type_I, Type_R;

  Comparator #(.width(6), .mode("unsigned")) comparator_1 (
    .a(Op_Code), .b({6{1'b0}}), .gt(OP___0_t), .eq(OP___0));  // open: lt
  Comparator #(.width(6), .mode("unsigned")) comparator_2 (.a(Op_Code), .b({6{1'b1}}), .eq(OP___63));  // open: gt, lt
  and and_1 (HiLo_Sel, OP___0, comparator_3_eq);
  Comparator #(.width(6), .mode("unsigned")) comparator_3 (
    .a(Func_Code), .b(6'b010010), .eq(comparator_3_eq));  // open: gt, lt
  and and_2 (mfhi, OP___0, comparator_4_eq);
  Comparator #(.width(6), .mode("unsigned")) comparator_4 (
    .a(Func_Code), .b(6'b010000), .eq(comparator_4_eq));  // open: gt, lt
  and and_3 (Halt, OP___63, comparator_5_eq);
  Comparator #(.width(6), .mode("unsigned")) comparator_5 (
    .a(Func_Code), .b({6{1'b1}}), .eq(comparator_5_eq));  // open: gt, lt
  Comparator #(.width(6), .mode("unsigned")) comparator_6 (
    .a(Func_Code), .b(6'b000001), .eq(comparator_6_eq), .lt(FC___1));  // open: gt
  and and_4 (tty, OP___63, comparator_6_eq);
  Comparator #(.width(6), .mode("unsigned")) comparator_7 (
    .a(Func_Code), .b(6'b011100), .lt(comparator_7_lt));  // open: gt, eq
  Comparator #(.width(6), .mode("unsigned")) comparator_8 (
    .a(Func_Code), .b(6'b010111), .gt(comparator_8_gt));  // open: eq, lt
  Comparator #(.width(6), .mode("unsigned")) comparator_9 (
    .a(Op_Code), .b(6'b001000), .lt(comparator_9_lt));  // open: gt, eq
  not not_1 (not_1_out, comparator_9_lt);
  Comparator #(.width(6), .mode("unsigned")) comparator_10 (
    .a(Op_Code), .b(6'b111000), .eq(comparator_10_eq));  // open: gt, lt
  and and_5 (Load_HiLo, OP___0, R, and_6_out);
  and and_6 (and_6_out, comparator_7_lt, comparator_8_gt);
  and and_7 (Type_I, OP___0_t, I, not_1_out);
  and and_8 (Pop, comparator_10_eq, FC___1);
  and and_9 (Push, comparator_10_eq, comparator_6_eq);
  Comparator #(.width(6), .mode("unsigned")) comparator_11 (
    .a(Func_Code), .b(6'b001000), .eq(comparator_11_eq));  // open: gt, lt
  Comparator #(.width(6), .mode("unsigned")) comparator_12 (
    .a(Func_Code), .b(6'b011111), .gt(comparator_12_gt));  // open: eq, lt
  Comparator #(.width(6), .mode("unsigned")) comparator_13 (
    .a(Func_Code), .b(6'b101100), .lt(comparator_13_lt));  // open: gt, eq
  and and_10 (Jr, OP___0, comparator_11_eq);
  // Probe on 6'b100011
  and and_11 (and_11_out, comparator_12_gt, comparator_13_lt);
  or or_1 (RF_R_W, rnd, lw, Type_I, Pop, HiLo_Sel, mfhi, Type_R, Push, KBD_En);
  or or_2 (R_Ram, lw, Pop);
  Comparator #(.width(6), .mode("unsigned")) comparator_14 (.a(Op_Code), .b(6'b100011), .eq(lw));  // open: gt, lt
  and and_12 (Type_R, OP___0, R, and_11_out);
  or or_3 (W_Ram, sw, Push);
  Comparator #(.width(6), .mode("unsigned")) comparator_15 (.a(Op_Code), .b(6'b101011), .eq(sw));  // open: gt, lt
  or or_4 (or_4_out, lw, Pop);
  Comparator #(.width(6), .mode("unsigned")) comparator_16 (
    .a(Func_Code), .b(6'b000010), .eq(comparator_16_eq));  // open: gt, lt
  nor nor_1 (nor_1_out, rnd, rnd, rnd);
  and and_13 (rnd, OP___63, comparator_16_eq);
  and and_14 (KBD_En, OP___63, comparator_17_eq);
  Comparator #(.width(6), .mode("unsigned")) comparator_17 (
    .a(Func_Code), .b(6'b000011), .eq(comparator_17_eq));  // open: gt, lt
  Priority_Encoder #(.select(2), .disabled(0)) priority_encoder_1 (
    .in0(nor_1_out), .in1(KBD_En), .in2(or_4_out), .in3(rnd), .out(RF_Sel));  // open: gs, en_out, en_in

  // Other names for the same wires on the sheet: FUNC[5:0] = Func_Code; kbd = KBD_En; mflo = HiLo_Sel;
  //   OP[5:0] = Op_Code
endmodule

module DataPath___main (
  input  in_1,
  input  [3:0] in_2,
  input  [31:0] in_3,
  input  in_4,
  input  [1:0] in_5,
  input  in_6,
  input  [1:0] in_7,
  input  [31:0] in_8,
  input  in_9,
  input  in_10,
  input  [1:0] in_11,
  input  in_12,
  input  [31:0] in_13,
  input  in_14,
  input  in_15,
  input  in_16,
  input  in_17,
  input  in_18,
  input  in_19,
  input  [31:0] in_20,
  input  in_21,
  input  in_22,
  input  [6:0] in_23,
  input  in_24,
  output [5:0] out_25,
  output [5:0] out_26,
  output [6:0] TTY_DATA,
  output [31:0] D_RAM_OUT,
  output out_29,
  output out_30,
  output out_31,
  output [15:0] RAM_DIR,
  output [3:0] MASK
);

  wire and_1_out, and_2_out, and_3_out, and_4_out, FC, jmp, N, or_1_out, Z;
  wire [4:0] A3, multiplexer_4_out, Rd, Rs, Rt;
  wire [6:0] demultiplexer_1_out0, undriven;
  wire [15:0] k, Ram_adress, Ram_W_Adress;
  wire [27:0] D;
  wire [31:0] ALU_Hi, ALU_OUT, ALU_Out_t, B, branch_control_1_ia_prime, \const , DIR, Hi, Hi_Lo, IA,
       instr_fetcher_1_data_from_ram, instruction, KBD_Out, Lo, multiplexer_1_out, multiplexer_2_out,
       multiplexer_3_out, multiplexer_7_out, multiplexer_10_out, multiplexer_11_out, Ram_Out, SP, ticks;
  wire [31:7] A;

  Multiplexer #(.width(32), .disabled(0), .enable("false")) multiplexer_1 (
    .in0(DIR), .in1({A, TTY_DATA}), .out(multiplexer_1_out), .sel(in_6));
  assign KBD_Out = {{25{1'b0}}, undriven};  // Bit_Extender bit_extender_1
  Demultiplexer #(.width(7), .disabled(0), .enable("false")) demultiplexer_1 (
    .out0(demultiplexer_1_out0), .out1(in_23), .in(undriven), .sel(in_24));
  and and_1 (and_1_out, in_16, in_22);
  Flag_Condition_Switch flag_condition_switch_1 (.in_1(out_25), .in_2(Z), .in_3(N), .in_4(out_29), .FC(FC));
  Branch_Control branch_control_1 (
    .in_2(IA), .in_3(jmp), .in_4(FC), .IA_prime(branch_control_1_ia_prime), .in_1(multiplexer_1_out));
  Program_Counter program_counter_1 (
    .in_1(branch_control_1_ia_prime), .in_2(and_1_out), .in_3(in_21), .in_4(in_18), .out_5(IA));
  Multiplexer #(.width(32), .disabled(0), .enable("false")) multiplexer_2 (
    .in0(B), .in1({A, TTY_DATA}), .out(multiplexer_2_out), .sel(in_1));
  Multiplexer #(.width(32), .disabled(0), .enable("false")) multiplexer_3 (
    .in0(IA), .in1(ALU_OUT), .out(multiplexer_3_out), .sel(in_15));
  Constant_Completer constant_completer_1 (.in_1(out_25), .in_2(k), .\const (\const ));
  Instr_Fetcher instr_fetcher_1 (
    .in_1(in_3), .in_2(in_8), .in_3(in_13), .in_4(in_20), .in_5(multiplexer_3_out), .out_7(Ram_adress),
    .Data_From_RAM(instr_fetcher_1_data_from_ram));
  RAM_Storer ram_storer_1 (
    .in_1(multiplexer_2_out), .in_2(ALU_OUT), .value(D_RAM_OUT), .adr(Ram_W_Adress), .out_5(MASK));
  Multiplexer #(.width(5), .disabled(0), .enable("false")) multiplexer_4 (
    .in0(Rd), .in1(Rt), .out(multiplexer_4_out), .sel(out_29));
  or or_1 (or_1_out, in_1, in_4);
  Multiplexer #(.width(5), .disabled(0), .enable("false")) multiplexer_5 (
    .in0(multiplexer_4_out), .in1({5{1'b1}}), .out(A3), .sel(or_1_out));
  Register #(.width(32)) IR (.D(instr_fetcher_1_data_from_ram), .en(in_17), .Q(instruction), .clk(in_18), .clr(in_21));
  Register #(.width(32)) Data (.D(instr_fetcher_1_data_from_ram), .en(in_19), .Q(Ram_Out), .clk(in_18), .clr(in_21));
  Multiplexer #(.width(32), .disabled(0), .enable("false")) multiplexer_6 (
    .in0(\const ), .in1({IA[31:28], D}), .out(DIR), .sel(out_30));
  Multiplexer #(.select(2), .width(32), .disabled(0), .enable("false")) multiplexer_7 (
    .in0(ALU_Out_t), .in1(KBD_Out), .in2(Ram_Out), .in3(ticks), .out(multiplexer_7_out), .sel(in_11));
  and and_2 (and_2_out, in_9, in_16);
  or or_2 (jmp, in_6, out_30);
  Instruction_Decoder instruction_decoder_1 (
    .in_1(instruction), .I(out_29), .out_3(out_25), .J(out_30), .R(out_31), .func_code(out_26), .Rd(Rd),
    .Rt(Rt), .Rs(Rs), .Dest(D), .out_11(k));
  Register_File register_file_1 (
    .in_1(multiplexer_7_out), .DA(A3), .in_3(and_2_out), .SA(Rs), .in_5(in_21), .SB(Rt), .in_7(in_18),
    .A({A, TTY_DATA}), .B(B), .SP(SP));
  Multiplexer #(.width(16), .disabled(0), .enable("false")) multiplexer_8 (
    .in0(Ram_adress), .in1(Ram_W_Adress), .out(RAM_DIR), .sel(in_14));
  Multiplexer #(.width(32), .disabled(0), .enable("false")) multiplexer_9 (
    .in0(Hi), .in1(Lo), .out(Hi_Lo), .sel(in_12));
  Multiplexer #(.select(2), .width(32), .disabled(0), .enable("false")) multiplexer_10 (
    .in0(B), .in1(32'h4), .in2(\const ), .out(multiplexer_10_out), .sel(in_7));  // open: in3
  and and_3 (and_3_out, in_10, in_16);
  Multiplexer #(.select(2), .width(32), .disabled(0), .enable("false")) multiplexer_11 (
    .in0({A, TTY_DATA}), .in1(SP), .in2(Hi_Lo), .out(multiplexer_11_out), .sel(in_5));  // open: in3
  Register #(.width(32)) register_1 (.D(ALU_Hi), .en(and_3_out), .Q(Hi), .clk(in_18), .clr(in_21));
  Counter #(.width(32), .max('hffffffff)) Tick_Count (
    .count(1'b1), .Q(ticks), .clk(in_18));  // open: load, D, carry, clr
  ALU_2 alu_1 (
    .Output(ALU_OUT), .Z_Flag(Z), .Hi(ALU_Hi), .A(multiplexer_11_out), .B(multiplexer_10_out), .SEL(in_2),
    .N_Flagt(N));
  and and_4 (and_4_out, in_10, in_16);
  Register #(.width(32)) register_2 (.D(ALU_OUT), .en(and_4_out), .Q(Lo), .clk(in_18), .clr(in_21));
  // also tied to VCC on the sheet: {demultiplexer_1_out0[0], demultiplexer_1_out0[1], demultiplexer_1_out0[2], demultiplexer_1_out0[3], demultiplexer_1_out0[4], demultiplexer_1_out0[5], demultiplexer_1_out0[6]}

  // Other names for the same wires on the sheet: A[6:0] = TTY_DATA; ALU_Op[3:0] = in_2; ALU_SEL_A[1:0] = in_5;
  //   ALU_SEL_B[1:0] = in_7; clk = in_18; Data_Load = in_19; DATA_RAM_2[31:0] = in_8; DATA_RAM_3[31:0] = in_13;
  //   DATA_RAM_4[31:0] = in_20; DATA_RAM__1[31:0] = in_3; DATA_RAM_OUT[31:0] = D_RAM_OUT; Hi_Lo_Sel = in_12;
  //   HiLo_Load = in_10; I = out_29; I_or_D = in_15; IR_Load = in_17; J = out_30; J_Dir[31:0] = {IA[31:28], D};
  //   jr = in_6; KBD_AVAIBLE = in_24; KBD_D[6:0] = in_23; L_En = in_16; op_code[5:0] = out_25; PC_en = in_22;
  //   pop2 = in_4; push = in_1; R = out_31; RAM_RW = in_14; RF_D_SEL[1:0] = in_11; RF_R_W = in_9; rst = in_21

  // Notes on the sheet:
  //   RAM
endmodule

module Branch_Control (
  input  [31:0] in_1,
  input  [31:0] in_2,
  input  in_3,
  input  in_4,
  output [31:0] IA_prime
);

  wire [31:0] adder_1_out, IA_prime_prime, multip_con_signo_1_lo, multiplexer_1_out;

  Adder #(.width(32)) adder_1 (.a(in_2), .b(32'h4), .out(adder_1_out));  // open: cin, cout
  Multip_con_Signo multip_con_signo_1 (.A(in_1), .B(32'h4), .Lo(multip_con_signo_1_lo));  // open: Hi
  Multiplexer #(.width(32), .disabled(0), .enable("false")) multiplexer_1 (
    .in0({32{1'b0}}), .in1(multip_con_signo_1_lo), .out(multiplexer_1_out), .sel(in_4));
  Adder #(.width(32)) adder_2 (.a(adder_1_out), .b(multiplexer_1_out), .out(IA_prime_prime));  // open: cin, cout
  Multiplexer #(.width(32), .disabled(0), .enable("false")) multiplexer_2 (
    .in0(IA_prime_prime), .in1(in_1), .out(IA_prime), .sel(in_3));

  // Other names for the same wires on the sheet: FC = in_4; IA[31:0] = in_2; J_Size[31:0] = in_1; jmp = in_3

  // Notes on the sheet:
  //   BRANCH CONTROL
endmodule

module Flag_Condition_Switch (
  input  [5:0] in_1,
  input  in_2,
  input  in_3,
  input  in_4,
  output FC
);

  wire _000, A, and_1_out, and_6_out, B, beq, bgtz, blez, bltz, bne, C, D, E, nor_1_out, or_1_out, or_2_out;

  Decoder #(.select(3), .disabled(0), .enable("false")) decoder_1 (
    .out1(bltz), .out4(beq), .out5(bne), .out6(blez), .out7(bgtz), .sel(in_1[2:0]));  // open: out0, out2, out3
  Comparator #(.width(3)) comparator_1 (.a(in_1[5:3]), .b(3'b000), .eq(_000));  // open: gt, lt
  and and_1 (and_1_out, in_4, _000);
  and and_2 (A, bne, ~in_2);  // AND_Gate
  and and_3 (B, beq, in_2);
  and and_4 (C, blez, or_1_out);
  or or_1 (or_1_out, in_2, in_3);
  or or_2 (or_2_out, A, B, C, D, E);
  and and_5 (FC, or_2_out, and_1_out);
  nor nor_1 (nor_1_out, in_2, in_3);
  and and_6 (and_6_out, in_3, ~in_2);  // AND_Gate
  and and_7 (D, bgtz, nor_1_out);
  and and_8 (E, bltz, and_6_out);

  // Other names for the same wires on the sheet: I = in_4; N_Flag = in_3; Last_3[2:0] = in_1[2:0];
  //   op_code[5:0] = in_1; First_3[2:0] = in_1[5:3]; Z_Flag = in_2

  // Notes on the sheet:
  //   Flags Condition
endmodule

module Program_Counter (
  input  [31:0] in_1,
  input  in_2,
  input  in_3,
  input  in_4,
  output [31:0] out_5
);

  Register #(.width(32)) PC (.D(in_1), .en(in_2), .Q(out_5), .clk(in_4), .clr(in_3));

  // Other names for the same wires on the sheet: clk = in_4; en = in_2; PC[31:0] = out_5; PC_prime[31:0] = in_1;
  //   rst = in_3

  // Notes on the sheet:
  //   Program Counter
endmodule

module Instr_Fetcher (
  input  [31:0] in_1,
  input  [31:0] in_2,
  input  [31:0] in_3,
  input  [31:0] in_4,
  input  [31:0] in_5,
  output [31:0] Data_From_RAM,
  output [15:0] out_7
);

  Multiplexer #(.select(2), .width(32), .disabled(0), .enable("false")) multiplexer_1 (
    .in0(in_1), .in1(in_2), .in2(in_3), .in3(in_4), .out(Data_From_RAM), .sel(in_5[3:2]));

  assign out_7 = in_5[19:4];

  // Other names for the same wires on the sheet: adress[31:0] = in_5; DATA_SEL[1:0] = in_5[3:2];
  //   RAM_ADRESS[15:0] = in_5[19:4]; DATA_RAM_2[31:0] = in_2; DATA_RAM_3[31:0] = in_3; DATA_RAM_4[31:0] = in_4;
  //   DATA_RAM__1[31:0] = in_1

  // Notes on the sheet:
  //   RAM Fetcher
endmodule

module RAM_Storer (
  input  [31:0] in_1,
  input  [31:0] in_2,
  output [31:0] value,
  output [15:0] adr,
  output [3:0] out_5
);

  Multiplexer #(.select(2), .width(4), .disabled(0), .enable("false")) multiplexer_1 (
    .in0(4'b0001), .in1(4'b0010), .in2(4'b0100), .in3(4'b1000), .out(out_5), .sel(in_2[3:2]));

  assign adr = in_2[19:4];
  assign value = in_1;

  // Other names for the same wires on the sheet: dir[31:0] = in_2; MASK[1:0] = in_2[3:2]

  // Notes on the sheet:
  //   RAM STORER
endmodule

module Instruction_Decoder (
  input  [31:0] in_1,
  output I,
  output [5:0] out_3,
  output J,
  output R,
  output [5:0] func_code,
  output [4:0] Rd,
  output [4:0] Rt,
  output [4:0] Rs,
  output [27:0] Dest,
  output [15:0] out_11
);

  Type_Decoder type_decoder_1 (.in_1(in_1[31:26]), .I(I), .J(J), .R(R));

  assign Dest = {in_1[25:0], 2'b00};
  assign func_code = in_1[5:0];
  assign out_3 = in_1[31:26];
  assign out_11 = in_1[15:0];
  assign Rd = in_1[15:11];
  assign Rs = in_1[25:21];
  assign Rt = in_1[20:16];

  // Other names for the same wires on the sheet: D[25:0] = in_1[25:0]; instruct[31:0] = in_1; k[15:0] = in_1[15:0];
  //   op_code[5:0] = in_1[31:26]

  // Notes on the sheet:
  //   INSTRUCTION DECODER
endmodule

module Type_Decoder (
  input  [5:0] in_1,
  output I,
  output J,
  output R
);

  wire and_1_out, and_3_out, and_4_out, D___E___F___V___nD___nE___nF, nA___nB___nC, nD___nE___nF;

  nor nor_1 (nD___nE___nF, in_1[2], in_1[1], in_1[0]);
  and and_1 (and_1_out, in_1[2], in_1[1], in_1[0]);
  and and_2 (J, nA___nB___nC, ~in_1[2], in_1[1], ~in_1[0]);  // AND_Gate
  or or_1 (D___E___F___V___nD___nE___nF, nD___nE___nF, and_1_out);
  nor nor_2 (nA___nB___nC, in_1[5], in_1[4], in_1[3]);
  and and_3 (and_3_out, nA___nB___nC, nD___nE___nF);
  and and_4 (and_4_out, in_1[5], in_1[4], in_1[3], D___E___F___V___nD___nE___nF);
  or or_2 (R, and_3_out, and_4_out);
  nor nor_3 (I, J, R);

  // Other names for the same wires on the sheet: F = in_1[0]; E = in_1[1]; D = in_1[2]; C = in_1[3]; B = in_1[4];
  //   A = in_1[5]

  // Notes on the sheet:
  //   TYPE DECODER
endmodule

module Register_File (
  input  [31:0] in_1,
  input  [4:0] DA,
  input  in_3,
  input  [4:0] SA,
  input  in_5,
  input  [4:0] SB,
  input  in_7,
  output [31:0] A,
  output [31:0] SP,
  output [31:0] B
);

  wire a0, a1, a2, a3, a4, a5, a6, a7, a8, a9, a10, a11, a12, a13, a14, a15, a16, a17, a18, a19, a20, a21,
       a22, a23, a24, a25, a26, a27, a28, a29, a30, a31;
  wire [31:0] q0, q1, q2, q3, q4, q5, q6, q7, q8, q9, q10, q11, q12, q13, q14, q15, q16, q17, q18, q19, q20,
       q21, q22, q23, q24, q25, q26, q27, q28, q29, q30;

  Decoder #(.select(5), .disabled(0)) decoder_1 (
    .out0(a0), .out1(a1), .out2(a2), .out3(a3), .out4(a4), .out5(a5), .out6(a6), .out7(a7), .out8(a8),
    .out9(a9), .out10(a10), .out11(a11), .out12(a12), .out13(a13), .out14(a14), .out15(a15), .out16(a31),
    .out17(a30), .out18(a29), .out19(a28), .out20(a27), .out21(a26), .out22(a25), .out23(a24), .out24(a23),
    .out25(a22), .out26(a21), .out27(a20), .out28(a19), .out29(a18), .out30(a17), .out31(a16), .sel(DA),
    .en(in_3));
  Register #(.width(32)) R0 (.D({32{1'b0}}), .en(a0), .Q(q0), .clk(in_7), .clr(in_5));
  Register #(.width(32)) R4 (.D(in_1), .en(a4), .Q(q4), .clk(in_7), .clr(in_5));
  Register #(.width(32)) R8 (.D(in_1), .en(a8), .Q(q8), .clk(in_7), .clr(in_5));
  Register #(.width(32)) R12 (.D(in_1), .en(a12), .Q(q12), .clk(in_7), .clr(in_5));
  Register #(.width(32)) R16 (.D(in_1), .en(a16), .Q(q16), .clk(in_7), .clr(in_5));
  Register #(.width(32)) R20 (.D(in_1), .en(a20), .Q(q20), .clk(in_7), .clr(in_5));
  Register #(.width(32)) R24 (.D(in_1), .en(a24), .Q(q24), .clk(in_7), .clr(in_5));
  Register #(.width(32)) R28 (.D(in_1), .en(a28), .Q(q28), .clk(in_7), .clr(in_5));
  Register #(.width(32)) R1 (.D(in_1), .en(a1), .Q(q1), .clk(in_7), .clr(in_5));
  Register #(.width(32)) R5 (.D(in_1), .en(a5), .Q(q5), .clk(in_7), .clr(in_5));
  Register #(.width(32)) R9 (.D(in_1), .en(a9), .Q(q9), .clk(in_7), .clr(in_5));
  Register #(.width(32)) R13 (.D(in_1), .en(a13), .Q(q13), .clk(in_7), .clr(in_5));
  Register #(.width(32)) R17 (.D(in_1), .en(a17), .Q(q17), .clk(in_7), .clr(in_5));
  Register #(.width(32)) R21 (.D(in_1), .en(a21), .Q(q21), .clk(in_7), .clr(in_5));
  Register #(.width(32)) R25 (.D(in_1), .en(a25), .Q(q25), .clk(in_7), .clr(in_5));
  Register #(.width(32)) R29 (.D(in_1), .en(a29), .Q(q29), .clk(in_7), .clr(in_5));
  Register #(.width(32)) R2 (.D(in_1), .en(a2), .Q(q2), .clk(in_7), .clr(in_5));
  Register #(.width(32)) R6 (.D(in_1), .en(a6), .Q(q6), .clk(in_7), .clr(in_5));
  Register #(.width(32)) R10 (.D(in_1), .en(a10), .Q(q10), .clk(in_7), .clr(in_5));
  Register #(.width(32)) R14 (.D(in_1), .en(a14), .Q(q14), .clk(in_7), .clr(in_5));
  Register #(.width(32)) R18 (.D(in_1), .en(a18), .Q(q18), .clk(in_7), .clr(in_5));
  Register #(.width(32)) R22 (.D(in_1), .en(a22), .Q(q22), .clk(in_7), .clr(in_5));
  Register #(.width(32)) R26 (.D(in_1), .en(a26), .Q(q26), .clk(in_7), .clr(in_5));
  Register #(.width(32)) R30 (.D(in_1), .en(a30), .Q(q30), .clk(in_7), .clr(in_5));
  Register #(.width(32)) R3 (.D(in_1), .en(a3), .Q(q3), .clk(in_7), .clr(in_5));
  Register #(.width(32)) R7 (.D(in_1), .en(a7), .Q(q7), .clk(in_7), .clr(in_5));
  Register #(.width(32)) R11 (.D(in_1), .en(a11), .Q(q11), .clk(in_7), .clr(in_5));
  Register #(.width(32)) R15 (.D(in_1), .en(a15), .Q(q15), .clk(in_7), .clr(in_5));
  Register #(.width(32)) R19 (.D(in_1), .en(a19), .Q(q19), .clk(in_7), .clr(in_5));
  Register #(.width(32)) R23 (.D(in_1), .en(a23), .Q(q23), .clk(in_7), .clr(in_5));
  Register #(.width(32)) R27 (.D(in_1), .en(a27), .Q(q27), .clk(in_7), .clr(in_5));
  Register #(.width(32)) R31 (.D(in_1), .en(a31), .Q(SP), .clk(in_7), .clr(in_5));
  Multiplexer #(.select(5), .width(32), .enable("false")) multiplexer_1 (
    .in0(q0), .in1(q1), .in2(q2), .in3(q3), .in4(q4), .in5(q5), .in6(q6), .in7(q7), .in8(q8), .in9(q9),
    .in10(q10), .in11(q11), .in12(q12), .in13(q13), .in14(q14), .in15(q15), .in16(q16), .in17(q17),
    .in18(q18), .in19(q19), .in20(q20), .in21(q21), .in22(q22), .in23(q23), .in24(q24), .in25(q25),
    .in26(q26), .in27(q27), .in28(q28), .in29(q29), .in30(q30), .in31(SP), .out(A), .sel(SA));
  Multiplexer #(.select(5), .width(32), .enable("false")) multiplexer_2 (
    .in0(q0), .in1(q1), .in2(q2), .in3(q3), .in4(q4), .in5(q5), .in6(q6), .in7(q7), .in8(q8), .in9(q9),
    .in10(q10), .in11(q11), .in12(q12), .in13(q13), .in14(q14), .in15(q15), .in16(q16), .in17(q17),
    .in18(q18), .in19(q19), .in20(q20), .in21(q21), .in22(q22), .in23(q23), .in24(q24), .in25(q25),
    .in26(q26), .in27(q27), .in28(q28), .in29(q29), .in30(q30), .in31(SP), .out(B), .sel(SB));

  // Other names for the same wires on the sheet: clk = in_7; DI[31:0] = in_1; q31[31:0] = SP; R_W = in_3; rst = in_5

  // Notes on the sheet:
  //   REGISTER FILE
  //   Control Signals
  //   Input Register
  //   Registers
  //   Output Registers
endmodule

module ALU_2 (
  input  [31:0] A,
  input  [31:0] B,
  input  [3:0] SEL,
  output [31:0] Output,
  output Z_Flag,
  output N_Flagt,
  output [31:0] Hi
);

  wire comparator_1_lt, comparator_2_lt;
  wire [31:0] adder_1_out, and_1_out, bit_extender_1_out, bit_extender_2_out, divider_1_out,
       divisor_con_signo_1_div, Hi_Sign, Hi_t, multip_con_signo_1_lo, multiplier_1_out, nor_1_out, or_1_out,
       Rest, Rest_Sign, subtractor_1_out, xor_1_out;

  Adder #(.width(32)) adder_1 (.a(A), .b(B), .out(adder_1_out));  // open: cin, cout
  Subtractor #(.width(32)) subtractor_1 (.a(A), .b(B), .out(subtractor_1_out));  // open: bin, bout
  assign and_1_out = A & B;  // AND_Gate and_1, 32 bits wide
  assign or_1_out = A | B;  // OR_Gate or_1, 32 bits wide
  assign xor_1_out = A ^ B;  // XOR_Gate xor_1, 32 bits wide
  assign nor_1_out = ~(A | B);  // NOR_Gate nor_1, 32 bits wide
  Multiplier #(.width(32)) multiplier_1 (.a(A), .b(B), .out(multiplier_1_out), .cout(Hi_t));  // open: cin
  Multip_con_Signo multip_con_signo_1 (.A(A), .B(B), .Lo(multip_con_signo_1_lo), .Hi(Hi_Sign));
  Divider #(.width(32)) divider_1 (.a(A), .b(B), .out(divider_1_out), .rem(Rest));  // open: upper
  Divisor_con_Signo divisor_con_signo_1 (.A(A), .B(B), .Div(divisor_con_signo_1_div), .Rest(Rest_Sign));
  Comparator #(.width(32)) comparator_1 (.a(A), .b(B), .lt(comparator_1_lt));  // open: gt, eq
  Comparator #(.width(32), .mode("unsigned")) comparator_2 (.a(A), .b(B), .lt(comparator_2_lt));  // open: gt, eq
  assign bit_extender_1_out = {{31{1'b0}}, comparator_1_lt};  // Bit_Extender bit_extender_1
  assign bit_extender_2_out = {{31{1'b0}}, comparator_2_lt};  // Bit_Extender bit_extender_2
  Multiplexer #(.select(4), .width(32), .enable("false")) multiplexer_1 (
    .in0(adder_1_out), .in2(subtractor_1_out), .in4(and_1_out), .in5(or_1_out), .in6(xor_1_out),
    .in7(nor_1_out), .in8(multiplier_1_out), .in9(multip_con_signo_1_lo), .in10(divider_1_out),
    .in11(divisor_con_signo_1_div), .in12(bit_extender_1_out), .in13(bit_extender_2_out), .in15(A),
    .out(Output), .sel(SEL));  // open: in1, in3, in14
  Multiplexer #(.select(2), .width(32), .enable("false")) multiplexer_2 (
    .in0(Hi_t), .in1(Hi_Sign), .in2(Rest), .in3(Rest_Sign), .out(Hi), .sel(SEL[1:0]));
  // Probe on SEL[1:0]
  Comparator #(.width(32)) comparator_3 (.a(Output), .b({32{1'b0}}), .eq(Z_Flag), .lt(N_Flagt));  // open: gt

  // Other names for the same wires on the sheet: Selector[3:0] = SEL

  // Notes on the sheet:
  //   ARITHMETIC LOGIC UNIT(ALU)
endmodule

module Divisor_con_Signo (
  input  [31:0] A,
  input  [31:0] B,
  output [31:0] Div,
  output [31:0] Rest
);

  wire [30:0] Com_a2_A, Com_a2_B, Current, multiplexer_1_out, multiplexer_2_out, negator_3_out;

  Negator #(.width(31)) negator_1 (.in(A[30:0]), .out(Com_a2_A));
  Negator #(.width(31)) negator_2 (.in(B[30:0]), .out(Com_a2_B));
  xor xor_1 (Div[31], B[31], A[31]);
  Multiplexer #(.width(31), .enable("false")) multiplexer_1 (
    .in0(A[30:0]), .in1(Com_a2_A), .out(multiplexer_1_out), .sel(A[31]));
  Multiplexer #(.width(31), .enable("false")) multiplexer_2 (
    .in0(B[30:0]), .in1(Com_a2_B), .out(multiplexer_2_out), .sel(B[31]));
  Negator #(.width(31)) negator_3 (.in(Current), .out(negator_3_out));
  Multiplexer #(.width(31), .enable("false")) multiplexer_3 (
    .in0(Current), .in1(negator_3_out), .out(Div[30:0]), .sel(Div[31]));
  Divider #(.width(31)) divider_1 (
    .a(multiplexer_1_out), .b(multiplexer_2_out), .out(Current), .rem(Rest[30:0]));  // open: upper

  assign Rest[31] = 1'b0;

  // Other names for the same wires on the sheet: A_t[30:0] = A[30:0]; Sign_A = A[31]; B_t[30:0] = B[30:0];
  //   Sign_B = B[31]; Div_t[30:0] = Div[30:0]; Sign = Div[31]; Rest_t[30:0] = Rest[30:0]

  // Notes on the sheet:
  //   Divisor Con Signo
endmodule

module Multip_con_Signo (
  input  [31:0] A,
  input  [31:0] B,
  output [31:0] Lo,
  output [31:0] Hi
);

  wire [30:0] Com_a2_A, Com_a2_B, multiplexer_1_out, multiplexer_2_out;

  Negator #(.width(31)) negator_1 (.in(A[30:0]), .out(Com_a2_A));
  Negator #(.width(31)) negator_2 (.in(B[30:0]), .out(Com_a2_B));
  xor xor_1 (Hi[31], B[31], A[31]);
  Multiplexer #(.width(31), .enable("false")) multiplexer_1 (
    .in0(A[30:0]), .in1(Com_a2_A), .out(multiplexer_1_out), .sel(A[31]));
  Multiplexer #(.width(31), .enable("false")) multiplexer_2 (
    .in0(B[30:0]), .in1(Com_a2_B), .out(multiplexer_2_out), .sel(B[31]));
  Multiplier #(.width(31)) multiplier_1 (
    .a(multiplexer_1_out), .b(multiplexer_2_out), .out(Lo[30:0]), .cout({Hi[29:0], Lo[31]}));  // open: cin

  assign Hi[30] = 1'b0;

  // Other names for the same wires on the sheet: A_t[30:0] = A[30:0]; Sign_A = A[31]; B_t[30:0] = B[30:0];
  //   Sign_B = B[31]; Hi_Mult[30:0] = {Hi[29:0], Lo[31]}; Sign = Hi[31]; Mult[30:0] = Lo[30:0]
endmodule

module Constant_Completer (
  input  [5:0] in_1,
  input  [15:0] in_2,
  output [31:0] \const 
);

  wire branch_comp, zero_comp;
  wire [31:0] multiplexer_1_out, sign_k, zero_k;
  wire [31:18] branch_k;

  assign branch_k = {{13{in_2[15]}}, in_2[15]};  // Bit_Extender bit_extender_1
  assign zero_k = {{16{1'b0}}, in_2};  // Bit_Extender bit_extender_2
  assign sign_k = {{16{in_2[15]}}, in_2};  // Bit_Extender bit_extender_3
  Comparator #(.width(3), .mode("unsigned")) comparator_1 (
    .a(in_1[5:3]), .b(3'b000), .eq(branch_comp));  // open: gt, lt
  Comparator #(.width(4), .mode("unsigned")) comparator_2 (.a(in_1[5:2]), .b(4'b0011), .eq(zero_comp));  // open: gt, lt
  Multiplexer #(.width(32), .disabled(0), .enable("false")) multiplexer_1 (
    .in0(sign_k), .in1({branch_k, in_2, 2'b00}), .out(multiplexer_1_out), .sel(branch_comp));
  Multiplexer #(.width(32), .disabled(0), .enable("false")) multiplexer_2 (
    .in0(multiplexer_1_out), .in1(zero_k), .out(\const ), .sel(zero_comp));

  // Other names for the same wires on the sheet: branch_k[17:2] = in_2; k[15:0] = in_2; k_15 = in_2[15];
  //   op_code[5:0] = in_1; First_4[3:0] = in_1[5:2]; First_3[2:0] = in_1[5:3]

  // Notes on the sheet:
  //   Constant Completer
endmodule
